# Fritzing sketch esp8266dht11clock (saved by Fritzing 0.9.3b)
breadboards: 1

parts:
  Gizwits_WiFi_Witty_ESP-12F1 = Gizwits WiFi Witty ESP-12F
  DHT1 = DHT11 Humitidy and Temperature Sensor
  R1 = Resistor [tolerance=±5% resistance=10k package=THT]
  S1 = Pushbutton [package="[THT]"]
  Part1 = gos_fixed_oled_128x32 [part_number=931]
  R2 = Resistor [tolerance=±5% resistance=10k package=THT]
  S2 = Pushbutton [package="[THT]"]

nets:
  N1: Gizwits_WiFi_Witty_ESP-12F1.REST, R2.Pin_1, S2.Pin_3, S2.Pin_4
  N2: Gizwits_WiFi_Witty_ESP-12F1.GPIO16, R1.Pin_1, S1.Pin_3, S1.Pin_4
  N3: Gizwits_WiFi_Witty_ESP-12F1.GPIO14, Part1.connector7
  N4: Gizwits_WiFi_Witty_ESP-12F1.GPIO13, Part1.connector8
  3.3V: Gizwits_WiFi_Witty_ESP-12F1.VCC, DHT1.VDD, R1.Pin_0, Part1.connector6, R2.Pin_0
  GND: Gizwits_WiFi_Witty_ESP-12F1.GND, DHT1.GND, S1.Pin_1, S1.Pin_2, Part1.connector5, S2.Pin_1, S2.Pin_2
  N5: Gizwits_WiFi_Witty_ESP-12F1.GPIO5, DHT1.DATA

custom parts:
  DHT11 Humitidy and Temperature Sensor: DHT11 Humidity and Temperature Sensor
