# Fritzing sketch complex (saved by Fritzing 0.9.3b)
perfboards: 1

parts:
  Part1 = Arduino Uno (Rev3)
  LED1 = LED - 5mm [color="Red (633nm)" package="5 mm [THT]"]
  LED2 = LED - 5mm [color="Blue (430nm)" package="5 mm [THT]"]
  LED3 = LED - 5mm [color="Green (555nm)" package="5 mm [THT]"]
  LED4 = LED - 5mm [color="Yellow (585nm)" package="5 mm [THT]"]
  R1 = Rotary Potentiometer (Small) [maximum_resistance=2.6k package=THT]
  J1 = Screw terminal - 2 pins [package=THT]
  J2 = male pin header, 2 pins [form="♂ (male)"]
  J3 = male pin header, 2 pins [form="♂ (male)"]
  J4 = male pin header, 3 pins [form="♂ (male)"]
  J5 = female pin header, 6 pins [form="♀ (female)"]
  J6 = female pin header, 4 pins [form="♀ (female)"]
  J7 = female pin header, 4 pins [form="♀ (female)"]
  R2 = Resistor [tolerance=±5% resistance=330 package=THT]
  R3 = Resistor [tolerance=±5% resistance=330 package=THT]
  R4 = Resistor [tolerance=±5% resistance=150 package=THT]
  R5 = Resistor [tolerance=±5% resistance=150 package=THT]
  J8 = male pin header, 2 pins [form="♂ (male)"]
  J9 = male pin header, 2 pins [form="♂ (male)"]
  S1 = Pushbutton [package="[THT]"]
  R6 = Resistor [tolerance=±5% resistance=10k package=THT]
  U1 = MAX485 [package=dil08]
  U2 = MAX6675 [package=so08]
  J10 = female pin header, 5 pins [form="♀ (female)"]
  J11 = female pin header, 8 pins [form="♀ (female)"]
  Part2 = Adafruit MAX31865 RTD Sensor Breakout [part_number="Adafruit #3328"]
  J12 = male pin header, 2 pins [form="♂ (male)"]

nets:
  N1: Part1.A0, S1.Pin_1, S1.Pin_2, R6.Pin_0
  N2: Part1.A1, J4.pin1
  N3: Part1.A2, R1.wiper, J4.pin2
  N4: Part1.A3, J4.pin3
  N5: Part1.A4/SDA, J7.pin4
  N6: Part1.A5/SCL, J7.pin3
  N7: Part1.D8, U2.CS, J10.pin4
  N8: Part1.D9_PWM, J12.pin2
  N9: Part1.D10_PWM/SS, J12.pin1
  N10: Part1.D11_PWM/MOSI, J11.pin2, Part2.SDI
  N11: Part1.D12/MISO, U2.MISO, J10.pin3, J11.pin5, Part2.SDO
  N12: Part1.D13/SCK, U2.SCK, J10.pin5, J11.pin3, Part2.SCLK
  GND: Part1.GND, LED1.cathode, LED2.cathode, LED3.cathode, LED4.cathode, R1.leg1, J1.pin2, J2.pin2, J3.pin1, J5.pin1, J7.pin1, J8.pin1, J8.pin2, S1.Pin_3, S1.Pin_4, U1.GND, U2.VSS, J10.pin1, J11.pin8, Part2.GND
  N13: Part1.D0/RX, J6.pin4, U1.RO
  N14: Part1.D1/TX, J6.pin1, U1.DI
  N15: Part1.D2, J6.pin2, J6.pin3, U1.RE, U1.DE
  N16: Part1.D3_PWM, R5.Pin_0
  N17: Part1.D4, R4.Pin_0
  N18: Part1.D5_PWM, R2.Pin_0
  N19: Part1.D6_PWM, J1.pin1, J2.pin1, R3.Pin_0
  N20: Part1.D7, J11.pin4, Part2.CS
  3.3V: Part1.3V3, J11.pin7, Part2.VIN, Part2.3.3V
  5V: Part1.5V, R1.leg2, J5.pin4, J7.pin2, J9.pin1, J9.pin2, R6.Pin_1, U1.VCC, U2.VDD, J10.pin2
  9V: Part1.VIN, J3.pin2
  N21: LED1.anode, R3.Pin_1
  N22: LED2.anode, R2.Pin_1
  N23: LED3.anode, R5.Pin_1
  N24: LED4.anode, R4.Pin_1
  N25: J5.pin2, U1.A
  N26: J5.pin3, U1.B

notes:
  J1 and J2
  PIN 1 Heater out (D6)
  PIN 2 GND
  J3
  PIN 1 GND
  PIN 2 Vin
  J4
  PIN 1 A1
  PIN 2 A2
  PIN 3 A3
  J5 J6 MAX 485
  PIN 1 GND PIN 1 DITX
  PIN 2 A PIN 2 DED2
  PIN 3 B PIN 3 RED2
  PIN 4 VCC PIN 4 RORX
  J7 OLED
  PIN 1 GND
  PIN 2 VCC
  PIN 3 SCL / A5
  PIN 4 SDA / A4
  J12
  PIN 1 D10
  PIN 2 D9
  J10 MAX6675
  PIN 1 GND
  PIN 2 VCC
  PIN 3 DO D12/MISO
  PIN 4 CS D8
  PIN 5 CLK D13/SCK
  J11 MAX31865
  PIN 1
  PIN 2 SDI D12/MISO
  PIN 3 SCLK D13/SCK
  PIN 4 CS D7
  PIN 5 SDO D11/MOSI
  PIN 6
  PIN 7 Vin
  PIN 8 GND
  LED
  D3 LED3 Green
  D4 LED4 Yellow
  D5 LED2 Blue
  D6 LED1 Red
  Push Button
  S1 A0
  J8 GND and J9 5V
  PIN 1 GND PIN 1 5V
  PIN 2 GND PIN 2 5V

custom parts:
  Adafruit MAX31865 RTD Sensor Breakout: For precision temperature sensing, nothing beats a Platinum RTD. Resistance temperature detectors (RTDs) are temperature sensors that contain a resistor that changes resistance value as its temperature changes, basically a kind of thermistor. In this sensor, the resistor is actually a small strip of Platinum with a resistance of 100 ohms at 0°C, thus the name PT100. Compared to most NTC/PTC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
